# Fritzing sketch Particle_FEWSNet-v20240627 (saved by Fritzing 0.9.10b)

parts:
  R1 = Resistor [tolerance=±5% resistance=1k power=0.25 package=THT]
  C1 = Ceramic Capacitor [capacitance=0.1mF package="100 mil [THT, multilayer]"]
  Part4 = SI1145 Digital UV Index + IR + Visible Light Sensor [part_number=1777]
  R2 = Resistor [tolerance=±5% resistance=1k power=0.25 package=THT]
  C2 = Ceramic Capacitor [capacitance=0.1mF package="100 mil [THT, multilayer]"]
  U4 = Honeywell SS451A [chip_label="Hall Effect Sensor" package=THT]
  U7 = Honeywell SS451A [chip_label="Hall Effect Sensor" package=THT]
  Part12 = OLED Monochrome 128x32 I2C [part_number=931]
  Boron2 = Particle Boron
  Part14 = Adafruit Adalogger FeatherWing [part_number="Adafruit #2922"]
  Part17 = Adafruit SHT31-D [part_number="Adafruit #2857"]
  Part18 = Adafruit VEML7700 STEMMA QT [part_number="Adafruit #5378"]
  X2 = USB Connectors [package=usb-a-s-nosilk-female]  # not connected
  BAT2 = Battery Holders [package=lipo-1100mAh]  # not connected
  JP3 = Header 2 [package=jst-2-pth-ns]  # not connected
  JP4 = Header 2 [package=jst-2-pth-ns]  # not connected
  Part19 = USB Mini-B Breakout [part_number=1764]  # not connected
  U8 = Honeywell SS451A [chip_label="Hall Effect Sensor" package=THT]
  R3 = Resistor [tolerance=±5% resistance=1k power=0.25 package=THT]
  C3 = Ceramic Capacitor [capacitance=0.1mF package="100 mil [THT, multilayer]"]
  Part20 = Adafruit BMP280 [part_number="Adafruit #2651"]
  Part21 = Adafruit BMP388 [part_number="Adafruit #3966"]
  Part22 = Adafruit BME280 [part_number="Adafruit #2652"]
  Part23 = Adafruit MCP9808 [part_number="Adafruit #5027"]
  Part24 = Adafruit HTU21D-F Temperature & Humidity Sensor [part_number="Adafruit #1899"]

nets:
  N1: R1.Pin_0, C1.1
  N2: R1.Pin_1, U7.pin3
  N3: C1.0, C2.0, U4.pin2, U7.pin2
  GND: Part4.GND, Part12.GND
  +3V3: Part4.+3V3, Part12.3.3V
  N4: R2.Pin_0, C2.1, U4.pin1, U7.pin1, U8.pin1, R3.Pin_0, C3.1
  N5: R2.Pin_1, U4.pin3
  N6: Boron2.SCK, Part14.SCK
  N7: Boron2.MO, Part14.MOSI
  N8: Boron2.MI, Part14.MISO
  N9: Boron2.D5, Part14.CS
  GND_2: Part17.GND, Part18.GND, Part20.GND, Part21.GND, Part22.GND, Part23.GND, Part24.GND
  VCC: Part17.VCC, Part18.VCC, Part20.VCC, Part21.VCC, Part22.VCC, Part23.VCC, Part24.VCC
  N10: Part17.SDA, Part18.SDA, Part20.SDI/SDA, Part20.CS, Part21.SDI/SDA, Part22.SDI/SDA, Part23.SDA, Part24.SDA
  N11: Part17.SCL, Part18.SCL, Part20.SCK/SCL, Part21.SCK/SCL, Part22.SCK/SCL, Part23.SCL, Part24.SCL
  N12: U8.pin2, C3.0
  N13: U8.pin3, R3.Pin_1

notes:
  MCP9808 High Accuracy Temperature Sensor
  I2C 7-bit address 0x18
  HTU21D-F Temperature & Humidity Sensor
  I2C 7-bit address 0x40
  Anemometer (A4)
  SS451A Omnipolar Digital Hall-effect Sensor
  Wind Vane (as5600-so_ek_ab)
  AS5600 Rotory Position Sensor
  I2C 7-bit address 0x36
  Adafruit SI1145
  Light Sensor
  I2C 7-bit address 0x60
  Rain Gauge 1 (A3)
  SS451A Omnipolar Digital Hall-effect Sensor
  Particle FEWSNet Schematic
  w/Grove Shield
  w/WatchDog
  v2024-06-27
  Adafruit OLED 128x32
  Display SSD1306
  I2C 7-bit address 0x3C
  Feather Adalogger Shield
  Pin - D5 SD CS
  Pin - SPI MOSI
  Pin - SPI MISO
  Pin - SPI CLK
  Pin - SDA
  Pin - SCL
  Console Enable Jumper
  Jump Pin D8 to Ground
  D5 = Used by SD Card Chip Select
  D8 = Serial Console (Ground Pin to Enable)
  D7 = On Board LED - Unused - Not on Grove Shield
  D6 = Unused - Not on Grove Shield
  D5 = SD Card Chip Select
  D4 = SPI1 MSIO - LoRa
  D3 = SPI1 MOSI - LoRa
  D2 = SPI1 SCK - LoRa
  D1 = I2C SCL
  D0 = I2C SDA
  A0 = WatchDog Monitor/Relay Reset Trigger
  A1 = WatchDog Monitor Heartbeat
  A2 = Interrupt For Rain Gauge 2
  A3 = Interrupt For Rain Gauge 1
  A4 = Interrupt For Anemometer (Wind Speed)
  A5 =
  D13 = SPIO CLK SD Card
  D12 = SPI0 MOSI SD Card
  D11 = SPI0 MISO SD Card
  D10 =
  D9 =
  BMP280
  Barometic Pressure
  Altitude Sensor
  Temperature
  I2C 7-bit address
  Default = 0x77
  SD0 to GND = 0x76
  G 3 S S
  N V D C
  D 3 A L
  G 3 D D
  N V 3 2
  D 3
  G 3 A A
  N V 1 0
  D 3
  G 3 D D
  N V 5 4
  D 3
  S S 3 G
  C D V N
  L A 3 D
  R T 3 G
  X X V N
  X X 3 D
  A A 3 G
  2 3 V N
  3 D
  A A 3 G
  4 5 V N
  3 D
  SHT31 Temperature & Humidy
  I2C address 0x44
  I2C address 0x45 ADR Pin High
  VEML7700 Lux Sensor
  I2C address 0x10
  HIH8000 Temperature & Humidy
  I2C address 0x27
  Large Lipo Battery
  Voltage Regulator
  Solar Panel
  5V TR TR HB
  WatchDog Monitor
  Rain Gauge 2 (A2)
  SS451A Omnipolar Digital Hall-effect Sensor
  BMP388
  Barometic Pressure
  Altitude Sensor
  Temperature
  I2C 7-bit address
  Default = 0x77
  SD0 to GND = 0x76
  Adafruit's Grove Shield FeatherWing for Particle Mesh
  BME288
  Barometic Pressure
  Altitude Sensor
  Temperature
  Humidity
  I2C 7-bit address
  Default = 0x76
  SD0 to GND = 0x77

custom parts:
  SI1145 Digital UV Index + IR + Visible Light Sensor: The SI1145 is a new sensor from SiLabs with a calibrated light sensing algorithm that can calculate UV Index. It doesn't contain an actual UV sensing element, instead it approximates it based on visible & IR light from the sun. We took this outside a couple days and compared the calculated UV index with the news-reported index and found it was very accurate! It's a digital sensor that works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
  Honeywell SS451A: Omnipolar Digital Hall-effect Sensor
  OLED Monochrome 128x32 I2C: These displays are small, only about 1" diagonal, but very readable due to the high contrast of an OLED display. This display is made of 128x32 individual white OLED pixels, each one is turned on or off by the controller chip. Because the display makes its own light, no backlight is required. This reduces the power required to run the OLED and is why the display has such high contrast; we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
  Particle Boron: The Boron LTE is a powerful LTE CAT-M1 enabled development kit that can act as either a standalone cellular device or LTE enabled gateway, repeater, or endpoint for a Particle Mesh networks. Equipped with the Nordic nRF52840 and u-blox SARA 410 processors, the Boron has built-in battery charging circuitry which makes it easier to connect a Li-Po battery and 20 mixed signal GPIOs to interface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
  Adafruit Adalogger FeatherWing: This is the Adalogger FeatherWing: it adds both a battery-backed Real Time Clock and micro SD card storage to any Feather main board. This FeatherWing will make it real easy to add datalogging to any of our existing Feathers. You get both an I2C real time clock (PCF8523) with 32KHz crystal and battery backup, and a microSD socket that connects to the SPI port pins (+ extra pin for CS). Tested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
  Adafruit SHT31-D: Sensirion Temperature/Humidity sensors are some of the finest & highest-accuracy devices you can get. And, finally we have some that have a true I2C interface for easy reading. The SHT31-D sensor has an excellent ±2% relative humidity and ±0.3°C accuracy for most uses. We now use the version with a PTFE filter, it'll stay clean while still allowing humidity measurements to work Unlike earlier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
  Adafruit VEML7700 STEMMA QT: Vishay has a lot of light sensors out there, and this is a nice simple lux sensor that's easy to add to any microcontoller. Most light sensors just give you a number for brighter/darker ambient lighting. The VEML7700 makes your life easier by calculating the lux, which is an SI unit for light. You'll get more consistent readings between multiple sensors because you aren't dealing with some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
  USB Mini-B Breakout: Simple but effective - this breakout board has a USB Mini-B connector, with all 5 pins broken out. Great for pairing with a microcontroller with USB support, or adding USB 5V power to a project.
  Adafruit BMP280: Bosch has stepped up their game with their new BMP280 sensor, an environmental sensor with temperature, barometric pressure that is the next generation upgrade to the BMP085/BMP180/BMP183. This sensor is great for all sorts of weather sensing and can even be used in both I2C and SPI! This precision sensor from Bosch is the best low-cost, precision sensing solution for measuring barometric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
  Adafruit BMP388: Bosch has been a leader in barometric pressure sensors, from the BMP085. BMP180, and BMP280... now we've got the next generation, the Adafruit BMP388 Precision Barometric Pressure sensor. As you would expect, this sensor is similar to its earlier versions but even better. The BMP388 has better precision than ever, which makes it excellent for environmental sensing or as a precision altimeter.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
  Adafruit BME280: Bosch has stepped up their game with their new BME280 sensor, an environmental sensor with temperature, barometric pressure and humidity! This sensor is great for all sorts of indoor environmental sensing and can even be used in both I2C and SPI! This precision sensor from Bosch is the best low-cost sensing solution for measuring humidity with ±3% accuracy, barometric pressure with ±1 hPa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
  Adafruit MCP9808: The MCP9808 digital temperature sensor is one of the more accurate/precise we've ever seen, with a typical accuracy of ±0.25°C over the sensor's -40°C to +125°C range and precision of +0.0625°C. They work great with any microcontroller using standard I2C. With three address jumpers on the back, you can connect up to 8 to a single I2C bus without address collisions. Best of all, a wide voltage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
  Adafruit HTU21D-F Temperature & Humidity Sensor: It's summer and you're sweating and your hair's all frizzy and all you really want to know is why the weatherman said this morning that today's relative humidity would max out at a perfectly reasonable 52% when it feels more like 77%. Enter the HTU21D-F Temperature + Humidity Sensor - the best way to prove the weatherman wrong! This I2C digital humidity sensor is an accurate and intelligent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
